# Fritzing sketch breadboard (saved by Fritzing 0.9.9b)
breadboards: 1

parts:
  MH-ET_LIVE_ESP32_DEVKIT1 = MH-ET LIVE ESP32 DEVKIT
  LED1 = LED - 3mm [color="Green (560nm)" current=0.030 package="3 mm [THT]"]
  LED2 = LED - 3mm [color="Red (633nm)" current=0.030 package="3 mm [THT]"]
  R1 = Resistor [tolerance=±5% resistance=220 package="2512 [SMD]"]
  R2 = Resistor [tolerance=±5% resistance=220 package="2512 [SMD]"]
  S1 = Pushbutton [package="[SMD]"]

nets:
  N1: MH-ET_LIVE_ESP32_DEVKIT1.connector65, R1.Pin_1
  N2: MH-ET_LIVE_ESP32_DEVKIT1.connector66, R2.Pin_1
  N3: MH-ET_LIVE_ESP32_DEVKIT1.connector70, LED1.cathode, LED2.cathode, S1.Pin_3, S1.Pin_4
  N4: MH-ET_LIVE_ESP32_DEVKIT1.connector73, S1.Pin_1, S1.Pin_2
  N5: LED1.anode, R1.Pin_0
  N6: LED2.anode, R2.Pin_0
